// Logisim project 7_Segment.circ as structural Verilog: 2 circuits, main circuit main
module main (
  input  D,
  input  C,
  input  B,
  input  A
);

  wire b2d_1_e, b2d_1_f, b2d_1_g, b2d_1_out_5, b2d_1_out_6, b2d_1_out_7, b2d_1_out_8;

  B2D b2d_1 (
    .D(D), .C(C), .B(B), .A(A), .out_5(b2d_1_out_5), .out_6(b2d_1_out_6), .out_7(b2d_1_out_7),
    .out_8(b2d_1_out_8), .e(b2d_1_e), .f(b2d_1_f), .g(b2d_1_g));
  _7_Segment_Display u_7_segment_display_1 (
    .g(b2d_1_g), .f(b2d_1_f), .a(b2d_1_out_5), .b(b2d_1_out_6), .e(b2d_1_e), .d(b2d_1_out_8), .c(b2d_1_out_7));  // open: dp
endmodule

module B2D (
  input  D,
  input  C,
  input  B,
  input  A,
  output out_5,
  output out_6,
  output out_7,
  output out_8,
  output e,
  output f,
  output g
);

  wire and_1_out, and_2_out, and_3_out, and_4_out, and_5_out, and_6_out, and_7_out, and_8_out, and_9_out,
       and_10_out, and_11_out, and_12_out, and_13_out, and_14_out, and_15_out, and_16_out, not_1_out,
       not_2_out, not_3_out;

  not not_1 (not_1_out, C);
  not not_2 (not_2_out, B);
  not not_3 (not_3_out, A);
  and and_1 (and_1_out, not_1_out, not_3_out);
  and and_2 (and_2_out, C, A);
  and and_3 (and_3_out, not_2_out, not_3_out);
  and and_4 (and_4_out, B, A);
  and and_5 (and_5_out, not_1_out, not_3_out);
  and and_6 (and_6_out, not_1_out, B);
  and and_7 (and_7_out, C, not_2_out, A);
  and and_8 (and_8_out, B, not_3_out);
  and and_9 (and_9_out, not_1_out, not_3_out);
  and and_10 (and_10_out, B, not_3_out);
  and and_11 (and_11_out, not_2_out, not_3_out);
  and and_12 (and_12_out, C, not_2_out);
  and and_13 (and_13_out, C, not_3_out);
  and and_14 (and_14_out, not_1_out, B);
  and and_15 (and_15_out, C, not_2_out);
  and and_16 (and_16_out, B, not_3_out);
  or or_1 (out_5, and_1_out, B, and_2_out, D);
  or or_2 (out_6, not_1_out, and_3_out, and_4_out);
  or or_3 (out_7, not_2_out, A, C);
  or or_4 (out_8, and_5_out, and_6_out, and_7_out, and_8_out, D);
  or or_5 (e, and_9_out, and_10_out);
  or or_6 (f, and_11_out, and_12_out, and_13_out, D);
  or or_7 (g, and_14_out, and_15_out, D, and_16_out);
endmodule
