// Logisim project DEMUX.circ as structural Verilog: 1 circuit, main circuit main
module main (
  input  Sel,
  input  A,
  output out_3,
  output out_4
);

  wire not_1_out;

  not not_1 (not_1_out, Sel);
  and and_1 (out_3, not_1_out, A);
  and and_2 (out_4, A, Sel);
endmodule
