// Logisim project FullAdder.circ as structural Verilog: 2 circuits, main circuit main
module main (
  input  in_1,
  input  in_2,
  input  in_3,
  input  in_4,
  input  in_5,
  input  in_6,
  input  in_7,
  input  in_8,
  input  in_9,
  input  in_10,
  input  in_11,
  input  in_12,
  input  in_13,
  input  in_14,
  input  in_15,
  input  in_16,
  input  in_17,
  output out_18,
  output out_19,
  output out_20,
  output out_21,
  output out_22,
  output out_23,
  output out_24,
  output out_25,
  output out_26
);

  wire full_adder_1_c_out, full_adder_2_c_out, full_adder_3_c_out, full_adder_4_c_out, full_adder_5_c_out,
       full_adder_6_c_out, full_adder_7_c_out;

  Full_Adder full_adder_1 (.A(in_1), .B(in_2), .C_in(in_3), .sum(out_18), .C_out(full_adder_1_c_out));
  Full_Adder full_adder_2 (.A(in_4), .B(in_5), .C_in(full_adder_1_c_out), .sum(out_19), .C_out(full_adder_2_c_out));
  Full_Adder full_adder_3 (.A(in_6), .B(in_7), .C_in(full_adder_2_c_out), .sum(out_20), .C_out(full_adder_3_c_out));
  Full_Adder full_adder_4 (.A(in_8), .B(in_9), .C_in(full_adder_3_c_out), .sum(out_21), .C_out(full_adder_4_c_out));
  Full_Adder full_adder_5 (.A(in_10), .B(in_11), .C_in(full_adder_4_c_out), .sum(out_22), .C_out(full_adder_5_c_out));
  Full_Adder full_adder_6 (.A(in_12), .B(in_13), .C_in(full_adder_5_c_out), .sum(out_23), .C_out(full_adder_6_c_out));
  Full_Adder full_adder_7 (.A(in_14), .B(in_15), .C_in(full_adder_6_c_out), .sum(out_24), .C_out(full_adder_7_c_out));
  Full_Adder full_adder_8 (.A(in_16), .B(in_17), .C_in(full_adder_7_c_out), .sum(out_25), .C_out(out_26));
endmodule

module Full_Adder (
  input  A,
  input  B,
  input  C_in,
  output sum,
  output C_out
);

  wire and_1_out, and_2_out, xor_1_out;

  xor xor_1 (xor_1_out, A, B);
  xor xor_2 (sum, xor_1_out, C_in);
  and and_1 (and_1_out, xor_1_out, C_in);
  and and_2 (and_2_out, B, A);
  or or_1 (C_out, and_1_out, and_2_out);
endmodule
