// Logisim project FullSubtractor.circ as structural Verilog: 2 circuits, main circuit main
module main (
  input  in_1,
  input  in_2,
  input  in_3,
  input  in_4,
  input  in_5,
  input  in_6,
  input  in_7,
  input  in_8,
  input  in_9,
  input  in_10,
  input  in_11,
  input  in_12,
  input  in_13,
  input  in_14,
  input  in_15,
  input  in_16,
  input  in_17,
  output out_18,
  output out_19,
  output out_20,
  output out_21,
  output out_22,
  output out_23,
  output out_24,
  output out_25,
  output out_26
);

  wire full_subtractor_1_borrow, full_subtractor_2_borrow, full_subtractor_3_borrow,
       full_subtractor_4_borrow, full_subtractor_5_borrow, full_subtractor_6_borrow, full_subtractor_7_borrow;

  Full_Subtractor full_subtractor_1 (
    .A(in_1), .B(in_2), .Borrow_In(in_3), .Diff(out_18), .Borrow(full_subtractor_1_borrow));
  Full_Subtractor full_subtractor_2 (
    .A(in_4), .B(in_5), .Borrow_In(full_subtractor_1_borrow), .Diff(out_19), .Borrow(full_subtractor_2_borrow));
  Full_Subtractor full_subtractor_3 (
    .A(in_6), .B(in_7), .Borrow_In(full_subtractor_2_borrow), .Diff(out_20), .Borrow(full_subtractor_3_borrow));
  Full_Subtractor full_subtractor_4 (
    .A(in_8), .B(in_9), .Borrow_In(full_subtractor_3_borrow), .Diff(out_21), .Borrow(full_subtractor_4_borrow));
  Full_Subtractor full_subtractor_5 (
    .A(in_10), .B(in_11), .Borrow_In(full_subtractor_4_borrow), .Diff(out_22),
    .Borrow(full_subtractor_5_borrow));
  Full_Subtractor full_subtractor_6 (
    .A(in_12), .B(in_13), .Borrow_In(full_subtractor_5_borrow), .Diff(out_23),
    .Borrow(full_subtractor_6_borrow));
  Full_Subtractor full_subtractor_7 (
    .A(in_14), .B(in_15), .Borrow_In(full_subtractor_6_borrow), .Diff(out_24),
    .Borrow(full_subtractor_7_borrow));
  Full_Subtractor full_subtractor_8 (
    .A(in_16), .B(in_17), .Borrow_In(full_subtractor_7_borrow), .Diff(out_25), .Borrow(out_26));
endmodule

module Full_Subtractor (
  input  A,
  input  B,
  input  Borrow_In,
  output Diff,
  output Borrow
);

  wire and_1_out, and_2_out, not_1_out, not_2_out, xor_1_out;

  xor xor_1 (xor_1_out, A, B);
  not not_1 (not_1_out, xor_1_out);
  not not_2 (not_2_out, A);
  xor xor_2 (Diff, xor_1_out, Borrow_In);
  and and_1 (and_1_out, not_1_out, Borrow_In);
  and and_2 (and_2_out, B, not_2_out);
  or or_1 (Borrow, and_1_out, and_2_out);
endmodule
