// Logisim project OR_Gate.circ as structural Verilog: 1 circuit, main circuit main
module main (
  input  D,
  input  C,
  input  B,
  input  A
);

  wire and_1_out, not_1_out, or_1_out;

  not not_1 (not_1_out, A);
  and and_1 (and_1_out, B, not_1_out);
  or or_1 (or_1_out, C, and_1_out);
  _7_Segment_Display u_7_segment_display_1 (.f(D));  // open: g, a, b, e, d, c, dp
endmodule
